// Logisim project ex31.circ as structural Verilog: 1 circuit, main circuit main
module main (
);

  wire and_1_out, and_2_out, and_3_out, clock_1_out, Eingang_0_out, Eingang_1_out, not_1_out, not_2_out,
       not_3_out, nZ_E0_E1_out, or_1_out, Zustand_q, Zustand_qn;

  Clock clock_1 (.out(clock_1_out));
  Button Eingang_0 (.out(Eingang_0_out));
  Button Eingang_1 (.out(Eingang_1_out));
  not not_1 (not_1_out, Eingang_0_out);
  not not_2 (not_2_out, Eingang_1_out);
  and nZ_E0_E1 (nZ_E0_E1_out, Eingang_0_out, Eingang_1_out, Zustand_qn, Zustand_qn);
  and and_1 (and_1_out, Zustand_q, Eingang_0_out, Eingang_1_out);
  and and_2 (and_2_out, Zustand_q, not_1_out, not_2_out);
  D_Flip_Flop Zustand (.clk(clock_1_out), .D(nZ_E0_E1_out), .Q(Zustand_q), .Qn(Zustand_qn));  // open: preset, en, reset
  not not_3 (not_3_out, Eingang_0_out);
  or or_1 (or_1_out, and_1_out, and_2_out);
  and and_3 (and_3_out, Zustand_q, not_3_out);
  Button Ausgang_0 (.out(or_1_out));
  Button Ausgang_1 (.out(and_3_out));
endmodule
