// Logisim project ex33.circ as structural Verilog: 1 circuit, main circuit main
module main (
);

  wire _0_0_0_0_out, _0_0_1_1_out, _0_0_x_1_out, _0_1_1_0_out, _1_0_0_1_out, _1_x_0_0_out, clock_1_out,
       not_1_out, not_2_out, not_3_out, not_4_out, or_1_out, or_2_out, or_3_out, or_4_out, Q1_qn, Q2_qn,
       Q3_qn, Q4_qn, x_0_0_0_out, x_0_0_1_out;
  wire [3:0] Q1_q;

  Clock clock_1 (.out(clock_1_out));
  and _0_0_x_1 (_0_0_x_1_out, Q1_qn, Q2_qn, Q1_q[3]);
  and x_0_0_1 (x_0_0_1_out, Q2_qn, Q3_qn, Q1_q[3]);
  and _0_1_1_0 (_0_1_1_0_out, Q1_qn, Q1_q[1], Q1_q[2], Q4_qn);
  and _0_0_0_0 (_0_0_0_0_out, Q1_qn, Q2_qn, Q3_qn, Q4_qn);
  and _0_0_1_1 (_0_0_1_1_out, Q1_qn, Q2_qn, Q1_q[2], Q1_q[3]);
  and x_0_0_0 (x_0_0_0_out, Q2_qn, Q3_qn, Q4_qn);
  and _1_x_0_0 (_1_x_0_0_out, Q1_q[0], Q3_qn, Q4_qn);
  and _1_0_0_1 (_1_0_0_1_out, Q1_q[0], Q2_qn, Q3_qn, Q1_q[3]);
  or or_1 (or_1_out, _0_1_1_0_out, x_0_0_1_out, _0_0_x_1_out);
  or or_2 (or_2_out, _1_0_0_1_out, _0_0_0_0_out, _0_0_1_1_out);
  or or_3 (or_3_out, x_0_0_0_out, _0_0_1_1_out);
  or or_4 (or_4_out, _0_1_1_0_out, _1_x_0_0_out, _0_0_1_1_out);
  not not_1 (not_1_out, or_1_out);
  not not_2 (not_2_out, or_2_out);
  not not_3 (not_3_out, or_3_out);
  not not_4 (not_4_out, or_4_out);
  J_K_Flip_Flop Q1 (
    .J(or_1_out), .clk(clock_1_out), .K(not_1_out), .Q(Q1_q[0]), .Qn(Q1_qn));  // open: preset, en, reset
  J_K_Flip_Flop Q2 (
    .J(or_2_out), .clk(clock_1_out), .K(not_2_out), .Q(Q1_q[1]), .Qn(Q2_qn));  // open: preset, en, reset
  J_K_Flip_Flop Q3 (
    .J(or_3_out), .clk(clock_1_out), .K(not_3_out), .Q(Q1_q[2]), .Qn(Q3_qn));  // open: preset, en, reset
  J_K_Flip_Flop Q4 (
    .J(or_4_out), .clk(clock_1_out), .K(not_4_out), .Q(Q1_q[3]), .Qn(Q4_qn));  // open: preset, en, reset
  Hex_Digit_Display hex_digit_display_1 (.value(Q1_q));  // open: dp
endmodule
